// Logisim project brokenquestionmark.circ as structural Verilog: 13 circuits, main circuit HCT193_UpDownCounter
module main (
  input  [7:0] DataBus,
  input  in_2,
  input  [23:0] AddressBus,
  input  Manual,
  input  Load,
  input  Inc,
  input  Out,
  input  Reset,
  input  IncID,
  input  DecID,
  input  LoadID,
  input  CO8,
  input  RO,
  input  RI,
  input  in_15,
  input  RCIn,
  input  Carry,
  input  Shift,
  input  ROut,
  input  Reset_2,
  input  BypassOut,
  input  Crement,
  input  NOT,
  input  Rotate,
  input  RIn,
  output [7:0] out_26,
  output [7:0] out_27,
  output [23:0] out_28,
  output [7:0] out_29
);

  wire address_module_1_clkout, address_module_1_ino, address_module_1_outo, address_module_1_rc,
       address_module_1_resetout, address_module_2_zsout, address_module_3_clkout, address_module_3_ino,
       address_module_3_outo, address_module_3_rc, address_module_3_resetout, address_module_3_zsout,
       button_1_out, clock_1_out, controlled_buffer_1_out, not_1_out, not_2_out, register_controller_1_p3,
       register_controller_1_p5, register_controller_1_p7, register_controller_1_p9,
       register_controller_1_p11, register_controller_1_p13, register_controller_1_p15,
       register_controller_1_p17, register_controller_1_p19, register_controller_1_p21,
       register_controller_1_p23, register_controller_1_p25, register_controller_1_p30,
       register_controller_1_p31, register_controller_1_p32, register_controller_1_p33,
       register_controller_1_p34, register_controller_1_p35, register_controller_1_p36,
       register_controller_1_p37, register_module_1_borrowout, register_module_1_carryout;
  wire [7:0] address_module_1_addressout, address_module_1_idout, address_module_2_out8out,
       address_module_3_addressout, address_module_3_idout, address_module_3_out8out,
       register_controller_1_p1, register_module_1_lho, register_module_1_out_2, register_module_1_rho;

  Button button_1 (.out(button_1_out));
  Clock clock_1 (.out(clock_1_out));
  not not_1 (not_1_out, Manual);
  assign controlled_buffer_1_out = not_1_out ? clock_1_out : 1'bz;  // Controlled_Buffer controlled_buffer_1
  assign controlled_buffer_1_out = Manual ? button_1_out : 1'bz;  // Controlled_Buffer controlled_buffer_2
  not not_2 (not_2_out, Out);
  assign out_28 = not_2_out ? AddressBus : 24'bz;  // Controlled_Buffer controlled_buffer_3
  RAM_Module ram_module_1 (
    .Address(out_28[15:0]), .DataIn(out_29), .Out(RO), .Write(RI), .DataOut(out_29),
    .CLK(controlled_buffer_1_out));
  assign out_29 = in_2 ? DataBus : 8'bz;  // Controlled_Buffer controlled_buffer_4
  Register_Module register_module_1 (
    .NOT(register_controller_1_p19), .Data(register_controller_1_p1), .Load(register_controller_1_p3),
    .Reset(register_controller_1_p25), .Dec(register_controller_1_p9), .Carry(register_controller_1_p21),
    .Inc(register_controller_1_p7), .Clk(register_controller_1_p23), .Enablei(register_controller_1_p31),
    .ShiftLeft(register_controller_1_p11), .ShiftRight(register_controller_1_p13),
    .RotL(register_controller_1_p15), .RotR(register_controller_1_p17),
    .BypassOuti(register_controller_1_p33), .Out(register_controller_1_p5), .LHSE(register_controller_1_p35),
    .RHSE(register_controller_1_p37), .BorrowOut(register_module_1_borrowout),
    .Out_2(register_module_1_out_2), .LHO(register_module_1_lho), .RHO(register_module_1_rho),
    .CarryOut(register_module_1_carryout));
  Register_Module register_module_2 (
    .NOT(register_controller_1_p19), .Data(register_controller_1_p1), .Load(register_controller_1_p3),
    .Reset(register_controller_1_p25), .Dec(register_controller_1_p9), .Carry(register_controller_1_p21),
    .Inc(register_controller_1_p7), .Clk(register_controller_1_p23), .Enablei(register_controller_1_p30),
    .ShiftLeft(register_controller_1_p11), .ShiftRight(register_controller_1_p13),
    .RotL(register_controller_1_p15), .RotR(register_controller_1_p17),
    .BypassOuti(register_controller_1_p32), .Out(register_controller_1_p5), .LHSE(register_controller_1_p34),
    .RHSE(register_controller_1_p36), .BorrowOut(register_module_1_borrowout),
    .Out_2(register_module_1_out_2), .LHO(register_module_1_lho), .RHO(register_module_1_rho),
    .CarryOut(register_module_1_carryout));
  // Register_Controller register_controller_1: pin names not known; wires that end beside it: register_controller_1_p1, out_29, register_controller_1_p3, out_29, register_controller_1_p5, BypassOut, register_controller_1_p7, controlled_buffer_1_out, register_controller_1_p9, RCIn, register_controller_1_p11, Crement, register_controller_1_p13, Carry, register_controller_1_p15, NOT, register_controller_1_p17, Shift, register_controller_1_p19, Rotate, register_controller_1_p21, ROut, register_controller_1_p23, RIn, register_controller_1_p25, Reset_2, register_module_1_carryout, register_module_1_borrowout, register_module_1_out_2, register_controller_1_p30, register_controller_1_p31, register_controller_1_p32, register_controller_1_p33, register_controller_1_p34, register_controller_1_p35, register_controller_1_p36, register_controller_1_p37, in_15
  Address_Module address_module_1 (
    .AddressIn(out_29), .Reset(Reset), .In(Load), .Inc(Inc), .Clk(controlled_buffer_1_out), .OutI(Out),
    .IDIn(out_27), .AddressOut(address_module_1_addressout), .Value(out_28[7:0]),
    .OutO(address_module_1_outo), .IDOut(address_module_1_idout), .InO(address_module_1_ino),
    .ResetOut(address_module_1_resetout), .ClkOut(address_module_1_clkout), .RC(address_module_1_rc),
    .ZSIn(address_module_3_zsout), .Out8In(address_module_3_out8out), .Out8Out(out_26));  // open: ZSOut
  Address_Module address_module_2 (
    .AddressIn(address_module_3_addressout), .Reset(address_module_3_resetout), .In(address_module_3_ino),
    .Inc(address_module_3_rc), .Clk(address_module_3_clkout), .OutI(address_module_3_outo),
    .IDIn(address_module_3_idout), .Value(out_28[23:16]), .ZSOut(address_module_2_zsout),
    .Out8Out(address_module_2_out8out));  // open: AddressOut, OutO, IDOut, InO, ResetOut, ClkOut, RC, ZSIn, Out8In
  Address_Module address_module_3 (
    .AddressIn(address_module_1_addressout), .Reset(address_module_1_resetout), .In(address_module_1_ino),
    .Inc(address_module_1_rc), .Clk(address_module_1_clkout), .OutI(address_module_1_outo),
    .IDIn(address_module_1_idout), .AddressOut(address_module_3_addressout), .Value(out_28[15:8]),
    .OutO(address_module_3_outo), .IDOut(address_module_3_idout), .InO(address_module_3_ino),
    .ResetOut(address_module_3_resetout), .ClkOut(address_module_3_clkout), .RC(address_module_3_rc),
    .ZSIn(address_module_2_zsout), .ZSOut(address_module_3_zsout), .Out8In(address_module_2_out8out),
    .Out8Out(address_module_3_out8out));
  Address_Controller address_controller_1 (
    .IDIn(out_29), .IDInc(IncID), .IDDec(DecID), .IDLoad(LoadID), .Clk(controlled_buffer_1_out), .CO8(CO8),
    .Data8In(out_26), .IDOut(out_27), .Data8Out(out_29));

  // Notes on the sheet:
  //   Logisim Display
endmodule

module HCT139_2to4LineDecoder (
  input  G1i,
  input  A1,
  input  B1,
  input  G2i,
  input  A2,
  input  B2,
  output Y10,
  output Y11,
  output Y12,
  output Y13,
  output Y20,
  output Y21,
  output Y22,
  output Y23
);

  wire not_1_out, not_2_out, not_3_out, not_4_out, not_5_out, not_6_out, not_7_out, not_8_out;

  not not_1 (not_1_out, G1i);
  not not_2 (not_2_out, A1);
  not not_3 (not_3_out, A1);
  not not_4 (not_4_out, B1);
  not not_5 (not_5_out, G2i);
  not not_6 (not_6_out, A2);
  not not_7 (not_7_out, A2);
  not not_8 (not_8_out, B2);
  nand nand_1 (Y10, not_1_out, not_2_out, not_4_out);
  nand nand_2 (Y11, not_1_out, A1, not_4_out);
  nand nand_3 (Y12, not_1_out, not_3_out, B1);
  nand nand_4 (Y13, not_1_out, A1, B1);
  nand nand_5 (Y20, not_5_out, not_6_out, not_8_out);
  nand nand_6 (Y21, not_5_out, A2, not_8_out);
  nand nand_7 (Y22, not_5_out, not_7_out, B2);
  nand nand_8 (Y23, not_5_out, A2, B2);
endmodule

module HC153_4To1MultiPlexer (
  input  E1i,
  input  D13,
  input  D12,
  input  D11,
  input  D10,
  input  S0,
  input  S1,
  input  D23,
  input  D22,
  input  D21,
  input  D20,
  input  E2i,
  output Y1,
  output Y2
);

  wire and_1_out, and_2_out, and_3_out, and_4_out, and_5_out, and_6_out, and_7_out, and_8_out, not_1_out,
       not_2_out, not_3_out, not_4_out, not_5_out, not_6_out;

  not not_1 (not_1_out, E1i);
  and and_1 (and_1_out, not_1_out, not_5_out, not_3_out, D13);
  and and_2 (and_2_out, not_1_out, not_2_out, not_5_out, D12);
  or or_1 (Y1, and_1_out, and_2_out, and_3_out, and_4_out);
  and and_3 (and_3_out, not_1_out, not_3_out, not_4_out, D11);
  and and_4 (and_4_out, not_1_out, not_2_out, not_4_out, D10);
  not not_2 (not_2_out, S0);
  not not_3 (not_3_out, not_2_out);
  not not_4 (not_4_out, S1);
  not not_5 (not_5_out, not_4_out);
  and and_5 (and_5_out, D23, not_3_out, not_5_out, not_6_out);
  and and_6 (and_6_out, D22, not_2_out, not_5_out, not_6_out);
  and and_7 (and_7_out, D21, not_4_out, not_3_out, not_6_out);
  or or_2 (Y2, and_5_out, and_6_out, and_7_out, and_8_out);
  not not_6 (not_6_out, E2i);
  and and_8 (and_8_out, D20, not_2_out, not_4_out, not_6_out);
endmodule

module HCT193_UpDownCounter (
  input  P0,
  input  P1,
  input  P2,
  input  P3,
  input  PLi,
  input  CPUi,
  input  CPDi,
  input  MR,
  output TCUi,
  output TCDi,
  output Q0,
  output Q1,
  output Q2,
  output Q3
);

  wire and_1_out, and_2_out, and_3_out, and_4_out, and_5_out, and_6_out, nand_1_out, nand_2_out, nand_3_out,
       nand_4_out, nand_5_out, nand_6_out, nand_7_out, nand_8_out, nor_1_out, nor_2_out, nor_3_out,
       nor_4_out, not_1_out, not_2_out, not_3_out, not_4_out, not_5_out, not_6_out, not_7_out, not_8_out,
       or_1_out, or_2_out, or_3_out, or_4_out, t_ff_1_qn, t_ff_2_qn, t_ff_3_qn, t_ff_4_qn;

  not not_1 (not_1_out, PLi);
  not not_2 (not_2_out, CPUi);
  not not_3 (not_3_out, CPDi);
  not not_4 (not_4_out, MR);
  nand nand_1 (nand_1_out, not_1_out, not_4_out, P0);
  T_Flip_Flop t_ff_1 (.T(nor_1_out), .clk(nor_1_out), .Q(Q0), .Qn(t_ff_1_qn), .reset(or_1_out), .preset(not_5_out));
  not not_5 (not_5_out, nand_1_out);
  nor nor_1 (nor_1_out, not_2_out, not_3_out);
  or or_1 (or_1_out, ~not_4_out, ~nand_2_out);  // OR_Gate
  nand nand_2 (nand_2_out, nand_1_out, not_1_out);
  and and_1 (and_1_out, not_2_out, Q0);
  and and_2 (and_2_out, t_ff_1_qn, not_3_out);
  T_Flip_Flop t_ff_2 (.T(nor_2_out), .clk(nor_2_out), .Q(Q1), .Qn(t_ff_2_qn), .reset(or_2_out), .preset(not_6_out));
  nor nor_2 (nor_2_out, and_1_out, and_2_out);
  nand nand_3 (nand_3_out, not_1_out, not_4_out, P1);
  nand nand_4 (nand_4_out, nand_3_out, not_1_out);
  not not_6 (not_6_out, nand_3_out);
  or or_2 (or_2_out, ~not_4_out, ~nand_4_out);  // OR_Gate
  and and_3 (and_3_out, not_2_out, Q0, Q1);
  and and_4 (and_4_out, t_ff_2_qn, t_ff_1_qn, not_3_out);
  nand nand_5 (nand_5_out, not_1_out, not_4_out, P2);
  T_Flip_Flop t_ff_3 (.T(nor_3_out), .clk(nor_3_out), .Q(Q2), .Qn(t_ff_3_qn), .reset(or_3_out), .preset(not_7_out));
  not not_7 (not_7_out, nand_5_out);
  nor nor_3 (nor_3_out, and_3_out, and_4_out);
  or or_3 (or_3_out, ~not_4_out, ~nand_6_out);  // OR_Gate
  nand nand_6 (nand_6_out, nand_5_out, not_1_out);
  and and_5 (and_5_out, not_2_out, Q1, Q0, Q2);
  T_Flip_Flop t_ff_4 (.T(nor_4_out), .clk(nor_4_out), .Q(Q3), .Qn(t_ff_4_qn), .reset(or_4_out), .preset(not_8_out));
  nor nor_4 (nor_4_out, and_5_out, and_6_out);
  and and_6 (and_6_out, t_ff_3_qn, t_ff_2_qn, t_ff_1_qn, not_3_out);
  nand nand_7 (nand_7_out, nand_8_out, not_1_out);
  nand nand_8 (nand_8_out, not_1_out, not_4_out, P3);
  not not_8 (not_8_out, nand_8_out);
  or or_4 (or_4_out, ~not_4_out, ~nand_7_out);  // OR_Gate
  nand nand_9 (TCUi, not_2_out, Q2, Q1, Q0, Q3);
  nand nand_10 (TCDi, not_3_out, t_ff_1_qn, t_ff_2_qn, t_ff_3_qn, t_ff_4_qn);
endmodule

module HCT283_Adder (
  input  CIn,
  input  [3:0] A,
  input  [3:0] B,
  output [3:0] S,
  output COut
);

  Adder #(.width(4)) adder_1 (.a(A), .b(B), .out(S), .cin(CIn), .cout(COut));
endmodule

module HCT574_OctalLatch (
  input  OEi,
  input  [7:0] D,
  input  CP,
  output [7:0] Q
);

  wire not_1_out;
  wire [7:0] register_1_q;

  Register register_1 (.D(D), .en(1'b1), .clk(CP), .Q(register_1_q), .clr(1'b0));
  not not_1 (not_1_out, OEi);
  assign Q = not_1_out ? register_1_q : 8'bz;  // Controlled_Buffer controlled_buffer_1
endmodule

module CY7C199_SRAM (
  input  [7:0] Input,
  input  [14:0] Address,
  input  WEi,
  input  CEi,
  input  OEi,
  output [7:0] Output
);

  wire and_1_out, and_2_out, not_1_out, not_2_out;
  wire [7:0] ram_1_data;

  and and_1 (and_1_out, ~WEi, ~CEi);  // AND_Gate
  and and_2 (and_2_out, ~CEi, ~OEi);  // AND_Gate
  RAM #(.addrWidth(15)) ram_1 (.addr(Address), .we(and_1_out), .oe(and_2_out), .clk(and_1_out), .data(ram_1_data));
  not not_1 (not_1_out, and_2_out);
  assign ram_1_data = not_1_out ? Input : 8'bz;  // Controlled_Buffer controlled_buffer_1
  not not_2 (not_2_out, not_1_out);
  assign Output = not_2_out ? ram_1_data : 8'bz;  // Controlled_Buffer controlled_buffer_2
endmodule

module Address_Module (
  input  [7:0] IDIn,
  input  [7:0] AddressIn,
  input  Reset,
  input  Clk,
  input  In,
  input  Inc,
  input  ZSIn,
  input  OutI,
  input  [7:0] Out8In,
  output [7:0] IDOut,
  output ResetOut,
  output [7:0] AddressOut,
  output InO,
  output ClkOut,
  output RC,
  output ZSOut,
  output [7:0] Value,
  output OutO,
  output [7:0] Out8Out
);

  wire and_1_out, and_2_out, hct193_updowncounter_1_tcdi, hct193_updowncounter_1_tcui,
       hct193_updowncounter_2_tcui, nand_1_out, nand_2_out, nor_1_out, not_1_out, not_2_out, not_3_out,
       not_4_out;
  wire [7:0] hct193_updowncounter_1_q0;

  not not_1 (not_1_out, Clk);
  not not_2 (not_2_out, not_1_out);
  not not_3 (not_3_out, not_2_out);
  and and_1 (and_1_out, IDIn[0], and_2_out);
  and and_2 (and_2_out, Clk, not_3_out);
  nand nand_1 (nand_1_out, Clk, Inc);
  and and_3 (ZSOut, nor_1_out, ZSIn);
  nand nand_2 (nand_2_out, and_1_out, In);
  nor nor_1 (nor_1_out, hct193_updowncounter_1_q0[0], hct193_updowncounter_1_q0[1], hct193_updowncounter_1_q0[2], hct193_updowncounter_1_q0[3], hct193_updowncounter_1_q0[5], hct193_updowncounter_1_q0[6], hct193_updowncounter_1_q0[7], hct193_updowncounter_1_q0[4]);
  Pull_Resistor #(.pull(1)) pull_resistor_1 (.node(ZSIn));
  HCT193_UpDownCounter hct193_updowncounter_1 (
    .P0(AddressIn[0]), .P1(AddressIn[1]), .P2(AddressIn[2]), .P3(AddressIn[3]), .PLi(nand_2_out),
    .CPUi(nand_1_out), .CPDi(1'b1), .MR(Reset), .TCUi(hct193_updowncounter_1_tcui),
    .TCDi(hct193_updowncounter_1_tcdi), .Q0(hct193_updowncounter_1_q0[0]), .Q1(hct193_updowncounter_1_q0[1]),
    .Q2(hct193_updowncounter_1_q0[2]), .Q3(hct193_updowncounter_1_q0[3]));
  assign Out8Out = IDIn[0] ? hct193_updowncounter_1_q0 : 8'bz;  // Controlled_Buffer controlled_buffer_1
  HCT193_UpDownCounter hct193_updowncounter_2 (
    .P0(AddressIn[4]), .P1(AddressIn[5]), .P2(AddressIn[7]), .P3(AddressIn[7]), .PLi(nand_2_out),
    .CPUi(hct193_updowncounter_1_tcui), .CPDi(hct193_updowncounter_1_tcdi), .MR(Reset),
    .TCUi(hct193_updowncounter_2_tcui), .Q0(hct193_updowncounter_1_q0[4]), .Q1(hct193_updowncounter_1_q0[5]),
    .Q2(hct193_updowncounter_1_q0[6]), .Q3(hct193_updowncounter_1_q0[7]));  // open: TCDi
  DotMatrix #(.matrixcols(8), .matrixrows(1)) dotmatrix_1 (
    .col0(hct193_updowncounter_1_q0[7]), .col1(hct193_updowncounter_1_q0[6]),
    .col2(hct193_updowncounter_1_q0[5]), .col3(hct193_updowncounter_1_q0[4]),
    .col4(hct193_updowncounter_1_q0[3]), .col5(hct193_updowncounter_1_q0[2]),
    .col6(hct193_updowncounter_1_q0[1]), .col7(hct193_updowncounter_1_q0[0]));
  assign Value = OutI ? hct193_updowncounter_1_q0 : 8'bz;  // Controlled_Buffer controlled_buffer_2
  not not_4 (not_4_out, IDIn[0]);
  assign Out8Out = not_4_out ? Out8In : 8'bz;  // Controlled_Buffer controlled_buffer_3
  not not_5 (RC, hct193_updowncounter_2_tcui);

  assign AddressIn[6] = AddressIn[7];
  assign AddressOut = {{2{AddressIn[7]}}, AddressIn[5:0]};
  assign ClkOut = Clk;
  assign IDOut = {IDIn[0], IDIn[7:1]};
  assign InO = In;
  assign OutO = OutI;
  assign ResetOut = Reset;

  // Notes on the sheet:
  //   ZSIn: pull=up
  //   Enable Line
  //   Logisim
endmodule

module Address_Controller (
  input  [7:0] IDIn,
  input  IDInc,
  input  IDDec,
  input  IDLoad,
  input  Clk,
  input  CO8,
  input  [7:0] Data8In,
  output [7:0] IDOut,
  output [7:0] Data8Out
);

  wire and_1_out, or_1_out, or_2_out;
  wire [7:0] controlled_buffer_1_out;

  or or_1 (or_1_out, IDInc, IDDec);
  assign {controlled_buffer_1_out[6:0], controlled_buffer_1_out[7]} = IDDec ? IDOut : 8'bz;  // Controlled_Buffer controlled_buffer_1
  assign controlled_buffer_1_out = IDLoad ? IDIn : 8'bz;  // Controlled_Buffer controlled_buffer_2
  or or_2 (or_2_out, or_1_out, IDLoad);
  and and_1 (and_1_out, or_2_out, Clk);
  assign Data8Out = CO8 ? Data8In : 8'bz;  // Controlled_Buffer controlled_buffer_3
  assign {controlled_buffer_1_out[0], controlled_buffer_1_out[7:1]} = IDInc ? IDOut : 8'bz;  // Controlled_Buffer controlled_buffer_4
  HCT574_OctalLatch hct574_octallatch_1 (.OEi(1'b0), .D(controlled_buffer_1_out), .CP(and_1_out), .Q(IDOut));
endmodule

module Register_Module (
  input  NOT,
  input  [7:0] Data,
  input  Load,
  input  Reset,
  input  Dec,
  input  Carry,
  input  Inc,
  input  Clk,
  input  Enablei,
  input  ShiftLeft,
  input  ShiftRight,
  input  RotL,
  input  RotR,
  input  BypassOuti,
  input  Out,
  input  LHSE,
  input  RHSE,
  output [7:0] Out_2,
  output [7:0] LHO,
  output [7:0] RHO,
  output BorrowOut,
  output CarryOut
);

  wire and_1_out, and_2_out, and_3_out, and_4_out, and_5_out, and_6_out, and_7_out, and_8_out, and_9_out,
       and_10_out, and_11_out, and_12_out, and_13_out, button_1_out, hc153_4to1multiplexer_1_y1,
       hc153_4to1multiplexer_1_y2, hct193_updowncounter_1_tcdi, hct193_updowncounter_1_tcui,
       hct193_updowncounter_2_tcdi, hct193_updowncounter_2_tcui, nand_1_out, nand_2_out, nand_3_out,
       nand_4_out, nand_5_out, nand_6_out, nand_7_out, nand_8_out, nor_1_out, nor_2_out, nor_3_out,
       nor_4_out, not_1_out, not_2_out, not_3_out, not_4_out, not_5_out, not_6_out, not_7_out, not_8_out,
       not_9_out, not_10_out, not_11_out, not_12_out, not_13_out, not_14_out, or_1_out, or_2_out, or_3_out,
       or_4_out, or_5_out, or_6_out, or_7_out, or_8_out, or_9_out, or_10_out, or_11_out, or_12_out,
       s_r_ff_1_q, s_r_ff_2_q;
  wire [1:0] controlled_buffer_5_out;
  wire [7:0] controlled_buffer_1_out, hct193_updowncounter_1_q0;
  wire [7:6] controlled_buffer_6_out;

  and and_1 (and_1_out, Dec, Carry);
  and and_2 (and_2_out, Carry, Inc);
  not not_1 (not_1_out, Enablei);
  assign controlled_buffer_1_out = and_3_out ? Data : 8'bz;  // Controlled_Buffer controlled_buffer_1
  and and_3 (and_3_out, not_1_out, Load);
  and and_4 (and_4_out, and_3_out, and_5_out);
  and and_5 (and_5_out, Clk, not_1_out);
  and and_6 (and_6_out, Out, not_1_out);
  not not_2 (not_2_out, LHSE);
  and and_7 (and_7_out, not_1_out, or_1_out);
  or or_1 (or_1_out, NOT, or_2_out);
  or or_2 (or_2_out, or_7_out, and_4_out);
  or or_3 (or_3_out, Reset, button_1_out);
  nand nand_1 (nand_1_out, and_1_out, and_5_out);
  Button button_1 (.out(button_1_out));
  nand nand_2 (nand_2_out, and_2_out, and_5_out);
  nand nand_3 (nand_3_out, BypassOuti, nor_1_out);
  nor nor_1 (nor_1_out, and_6_out, and_6_out);
  nor nor_2 (nor_2_out, RHSE, RHSE);
  not not_3 (not_3_out, and_7_out);
  not not_4 (not_4_out, not_3_out);
  not not_5 (not_5_out, not_4_out);
  HCT193_UpDownCounter hct193_updowncounter_1 (
    .P0(controlled_buffer_1_out[0]), .P1(controlled_buffer_1_out[1]), .P2(controlled_buffer_1_out[2]),
    .P3(controlled_buffer_1_out[3]), .PLi(nand_4_out), .CPUi(nand_2_out), .CPDi(nand_1_out), .MR(or_3_out),
    .TCUi(hct193_updowncounter_1_tcui), .TCDi(hct193_updowncounter_1_tcdi),
    .Q0(hct193_updowncounter_1_q0[0]), .Q1(hct193_updowncounter_1_q0[1]), .Q2(hct193_updowncounter_1_q0[2]),
    .Q3(hct193_updowncounter_1_q0[3]));
  nand nand_4 (nand_4_out, and_7_out, not_5_out);
  HCT193_UpDownCounter hct193_updowncounter_2 (
    .P0(controlled_buffer_1_out[4]), .P1(controlled_buffer_1_out[5]), .P2(controlled_buffer_1_out[6]),
    .P3(controlled_buffer_1_out[7]), .PLi(nand_4_out), .CPUi(hct193_updowncounter_1_tcui),
    .CPDi(hct193_updowncounter_1_tcdi), .MR(or_3_out), .TCUi(hct193_updowncounter_2_tcui),
    .TCDi(hct193_updowncounter_2_tcdi), .Q0(hct193_updowncounter_1_q0[4]), .Q1(hct193_updowncounter_1_q0[5]),
    .Q2(hct193_updowncounter_1_q0[6]), .Q3(hct193_updowncounter_1_q0[7]));
  assign Out_2 = nand_3_out ? hct193_updowncounter_1_q0 : 8'bz;  // Controlled_Buffer controlled_buffer_2
  assign LHO = not_2_out ? hct193_updowncounter_1_q0 : 8'bz;  // Controlled_Buffer controlled_buffer_3
  assign RHO = nor_2_out ? hct193_updowncounter_1_q0 : 8'bz;  // Controlled_Buffer controlled_buffer_4
  or or_4 (or_4_out, and_3_out, NOT);
  or or_5 (or_5_out, RotR, RotL);
  not not_6 (not_6_out, hct193_updowncounter_2_tcdi);
  or or_6 (or_6_out, not_7_out, or_10_out);
  assign controlled_buffer_1_out = NOT ? ~hct193_updowncounter_1_q0 : 8'bz;  // Controlled_Inverter controlled_inverter_1
  Transistor transistor_1 (.in(hc153_4to1multiplexer_1_y2), .out(controlled_buffer_1_out[0]), .gate(or_4_out));
  Transistor #(.gate("br")) transistor_2 (
    .in(hc153_4to1multiplexer_1_y1), .out(controlled_buffer_1_out[7]), .gate(or_4_out));
  or or_7 (or_7_out, or_5_out, or_8_out);
  or or_8 (or_8_out, ShiftRight, ShiftLeft);
  or or_9 (or_9_out, ShiftLeft, RotL);
  nor nor_3 (nor_3_out, RotL, RotR);
  and and_8 (and_8_out, ShiftLeft, hct193_updowncounter_1_q0[7]);
  not not_7 (not_7_out, nor_3_out);
  or or_10 (or_10_out, ShiftLeft, ShiftRight);
  or or_11 (or_11_out, or_6_out, Clk);
  not not_8 (not_8_out, or_11_out);
  not not_9 (not_9_out, not_8_out);
  HC153_4To1MultiPlexer hc153_4to1multiplexer_1 (
    .E1i(or_4_out), .D13(controlled_buffer_6_out[6]), .D12(Carry), .D11(controlled_buffer_6_out[6]),
    .D10(controlled_buffer_5_out[0]), .S0(or_9_out), .S1(nor_3_out), .D23(Carry),
    .D22(controlled_buffer_5_out[1]), .D21(controlled_buffer_6_out[7]), .D20(controlled_buffer_5_out[1]),
    .E2i(or_4_out), .Y1(hc153_4to1multiplexer_1_y1), .Y2(hc153_4to1multiplexer_1_y2));
  and and_9 (and_9_out, ShiftRight, hct193_updowncounter_1_q0[0]);
  and and_10 (and_10_out, or_11_out, not_10_out);
  not not_10 (not_10_out, not_9_out);
  and and_11 (and_11_out, ~or_4_out, or_12_out);  // AND_Gate
  or or_12 (or_12_out, ShiftLeft, RotL);
  assign {controlled_buffer_1_out[6:1], controlled_buffer_5_out} = nor_4_out ? hct193_updowncounter_1_q0 : 8'bz;  // Controlled_Buffer controlled_buffer_5
  nor nor_4 (nor_4_out, or_12_out, or_4_out);
  nand nand_5 (nand_5_out, and_8_out, and_10_out);
  not not_11 (not_11_out, nand_5_out);
  S_R_Flip_Flop s_r_ff_1 (.Q(s_r_ff_1_q), .reset(not_12_out), .preset(not_11_out));  // open: S, R, clk, Qn
  nand nand_6 (nand_6_out, nand_5_out, and_10_out);
  not not_12 (not_12_out, nand_6_out);
  nand nand_7 (nand_7_out, and_9_out, and_10_out);
  not not_13 (not_13_out, nand_7_out);
  S_R_Flip_Flop s_r_ff_2 (.Q(s_r_ff_2_q), .reset(not_14_out), .preset(not_13_out));  // open: S, R, clk, Qn
  not not_14 (not_14_out, nand_8_out);
  nand nand_8 (nand_8_out, nand_7_out, and_10_out);
  assign {controlled_buffer_6_out, controlled_buffer_1_out[6:1]} = and_11_out ? hct193_updowncounter_1_q0 : 8'bz;  // Controlled_Buffer controlled_buffer_6
  or or_13 (CarryOut, ~hct193_updowncounter_2_tcui, and_12_out);  // OR_Gate
  and and_12 (and_12_out, s_r_ff_1_q, not_1_out);
  or or_14 (BorrowOut, not_6_out, and_13_out);
  and and_13 (and_13_out, not_1_out, s_r_ff_2_q);

  // Notes on the sheet:
  //   Bus In
  //   NOT Op
  //   Main Bus Out
  //   ALU Buses Out
  //   Right Ops
  //   IGNORE NOTs
  //   Use NANDs for SR Latch
  //   Chip Count
  //   1 HC153
  //   2 HCT 193
  //   6 HC245
  //   Left Ops
  //   1 HCT240
  //   12 OR -- 3 Chips
  //   10 AND -- 3 Chips
  //   11 NOT -- 2 Chips
  //   9 NAND -- 3 Chip
  //   2 NOR -- 1 Chip
  //   Recount
endmodule

module Register_Controller (
  input  BypassedOuti,
  input  [7:0] DataBus,
  input  CLK,
  input  RControllerIn,
  input  Crement,
  input  CarryIn,
  input  NOT,
  input  Shift,
  input  ROut,
  input  RegisterCarry,
  input  RIn,
  input  RegisterBorrow,
  input  RReset,
  input  Rotate,
  input  [7:0] RegisterBusOut,
  output Enable0i,
  output Enable1i,
  output [7:0] DataBusIn,
  output Output0i,
  output Enable2i,
  output Output1i,
  output Enable3i,
  output Output2i,
  output CLKOut,
  output Output3i,
  output RHO0i,
  output Inc,
  output RHO1i,
  output Dec,
  output RHO2i,
  output RHO3i,
  output LHO0i,
  output CarryToReg,
  output LHO1i,
  output NOT_2,
  output LHO2i,
  output LHO3i,
  output SR,
  output Out,
  output SL,
  output CarryResult,
  output Load,
  output BorrowResult,
  output Reset,
  output RL,
  output RR,
  output [7:0] DataBusOut
);

  wire and_1_out, and_2_out, and_5_out, and_10_out, and_11_out, nand_1_out, not_1_out, not_2_out, not_3_out,
       not_4_out, not_5_out, not_6_out, not_7_out, not_8_out, or_1_out;
  wire [7:0] hct574_octallatch_1_q;

  not not_1 (not_1_out, not_3_out);
  not u_not_2 (not_2_out, CLK);
  not not_3 (not_3_out, not_2_out);
  not not_4 (not_4_out, BypassedOuti);
  HCT574_OctalLatch hct574_octallatch_1 (.OEi(1'b0), .D(DataBus), .CP(and_2_out), .Q(hct574_octallatch_1_q));
  and and_1 (and_1_out, CLK, not_1_out);
  and and_2 (and_2_out, and_1_out, RControllerIn);
  or or_1 (or_1_out, ROut, BypassedOuti);
  assign DataBusOut = or_1_out ? RegisterBusOut : 8'bz;  // Controlled_Buffer controlled_buffer_1
  not not_5 (not_5_out, hct574_octallatch_1_q[3]);
  not not_6 (not_6_out, not_5_out);
  not not_7 (not_7_out, not_6_out);
  and and_3 (Inc, hct574_octallatch_1_q[3], Crement);
  and and_4 (Dec, Crement, not_5_out);
  nand nand_1 (nand_1_out, hct574_octallatch_1_q[2], not_8_out);
  not not_8 (not_8_out, CarryIn);
  and and_5 (and_5_out, hct574_octallatch_1_q[2], CarryIn);
  and and_6 (SR, not_5_out, Shift);
  and and_7 (SL, Shift, not_6_out);
  and and_8 (RL, not_6_out, Rotate);
  and and_9 (RR, Rotate, not_7_out);
  and and_10 (and_10_out, Crement, nand_1_out);
  or or_2 (CarryToReg, and_10_out, and_11_out);
  and and_11 (and_11_out, and_5_out, Shift);
  and and_12 (CarryResult, RegisterCarry, hct574_octallatch_1_q[2]);
  and and_13 (BorrowResult, hct574_octallatch_1_q[2], RegisterBorrow);
  HCT139_2to4LineDecoder hct139_2to4linedecoder_1 (
    .G1i(not_4_out), .A1(hct574_octallatch_1_q[2]), .B1(hct574_octallatch_1_q[3]), .G2i(1'b0),
    .A2(hct574_octallatch_1_q[0]), .B2(hct574_octallatch_1_q[1]), .Y10(Output0i), .Y11(Output1i),
    .Y12(Output2i), .Y13(Output3i), .Y20(Enable0i), .Y21(Enable1i), .Y22(Enable2i), .Y23(Enable3i));
  HCT139_2to4LineDecoder hct139_2to4linedecoder_2 (
    .G1i(1'b0), .A1(hct574_octallatch_1_q[4]), .B1(hct574_octallatch_1_q[5]), .G2i(1'b0),
    .A2(hct574_octallatch_1_q[2]), .B2(hct574_octallatch_1_q[3]), .Y10(LHO0i), .Y11(LHO1i), .Y12(LHO2i),
    .Y13(LHO3i), .Y20(RHO0i), .Y21(RHO1i), .Y22(RHO2i), .Y23(RHO3i));

  assign CLKOut = CLK;
  assign DataBusIn = DataBus;
  assign Load = RIn;
  assign NOT_2 = NOT;
  assign Out = ROut;
  assign Reset = RReset;

  // Notes on the sheet:
  //   Logisim
endmodule

module RAM_Module (
  input  [15:0] Address,
  input  [7:0] DataIn,
  input  Out,
  input  Write,
  input  CLK,
  output [7:0] DataOut
);

  wire and_1_out, and_2_out, not_1_out, not_2_out, not_3_out, not_4_out, not_5_out, not_6_out;
  wire [7:0] controlled_buffer_1_out;

  assign controlled_buffer_1_out = not_2_out ? DataIn : 8'bz;  // Controlled_Buffer controlled_buffer_1
  not not_1 (not_1_out, Out);
  not not_2 (not_2_out, Out);
  not not_3 (not_3_out, CLK);
  CY7C199_SRAM cy7c199_sram_1 (
    .Input(controlled_buffer_1_out), .Address(Address[15:1]), .WEi(and_2_out), .CEi(Address[0]),
    .OEi(not_1_out), .Output(controlled_buffer_1_out));
  CY7C199_SRAM cy7c199_sram_2 (
    .Input(controlled_buffer_1_out), .Address(Address[15:1]), .WEi(and_2_out), .CEi(not_6_out),
    .OEi(not_1_out), .Output(controlled_buffer_1_out));
  assign DataOut = Out ? controlled_buffer_1_out : 8'bz;  // Controlled_Buffer controlled_buffer_2
  and and_1 (and_1_out, CLK, not_4_out);
  not not_4 (not_4_out, not_5_out);
  not not_5 (not_5_out, not_3_out);
  not not_6 (not_6_out, Address[0]);
  and and_2 (and_2_out, Write, and_1_out);
endmodule

module NOTES (
);

  Controlled_Buffer controlled_buffer_1 ();  // open: in, out, en
  Controlled_Inverter controlled_inverter_1 ();  // open: in, out, en
  // NOT_Gate not_1 is placed but not wired
  // AND_Gate and_1 is placed but not wired
  // OR_Gate or_1 is placed but not wired

  // Notes on the sheet:
  //   All             are 74hc245 
  //   All              are 74hct240 
  //   All             are 74hct04 
  //   All              are 74hct08 
  //   All              are 74hct32 
  //   This gotta go FAAAST
endmodule
